# Fritzing sketch TA7642_receiver (saved by Fritzing 0.9.3b)
perfboards: 1

parts:
  IC1 = IC, SIP package, 3 pins [chip_label=TA7642]
  C2 = Ceramic Capacitor [capacitance=100nF package="100 mil [THT, multilayer]"]
  C1 = Ceramic Capacitor [capacitance=270pF package="100 mil [THT, multilayer]"]
  L1 = Inductor [inductance=220µH part_number=07HCP package="400 mil [THT]"]
  L2 = Inductor [part_number=SMCC inductance=150µH package="400 mil [THT]"]
  R1 = Resistor [tolerance=±5% resistance=100k package=THT]
  R2 = Resistor [tolerance=±5% resistance=1k package=THT]
  C4 = Electrolytic Capacitor [capacitance=0.1mF voltage=16V package="100 mil [THT, electrolytic]"]
  R3 = Resistor [tolerance=±5% resistance=1k package=THT]
  C5 = Electrolytic Capacitor [capacitance=0.1mF voltage=16V package="100 mil [THT, electrolytic]"]
  R4 = Resistor [tolerance=±5% resistance=1k package=THT]
  D1 = Rectifier Diode [part_number=1N4148 package="300 mil [THT]"]
  PWM = female pin header, 1 pin [form="♀ (female)"]
  OUT = female pin header, 1 pin [form="♀ (female)"]
  C3 = Ceramic Capacitor [capacitance=100nF package="100 mil [THT, multilayer]"]

nets:
  GND: IC1.pin1, C1.0, L2.pin_1, C4.-, C5.-, C3.0
  N1: IC1.pin2, C2.1, R1.Pin_0
  N2: IC1.pin3, C3.1
  N3: C2.0, C1.1, L1.pin_1
  N4: L1.pin_0, L2.pin_0
  N5: R1.Pin_1, R2.Pin_0, OUT.pin1
  N6: R2.Pin_1, C4.+, R3.Pin_0
  N7: R3.Pin_1, C5.+, R4.Pin_0
  N8: R4.Pin_1, D1.cathode
  N9: D1.anode, PWM.pin1
